# Fritzing sketch Automated cooling system_IOT (saved by Fritzing 0.9.3b)
breadboards: 1

parts:
  R1 = Rotary Potentiometer (Small) [maximum_resistance=100kΩ package=THT]
  M1 = DC Motor
  Part1 = Arduino Uno (Rev3)
  Q1 = PNP-Transistor [package="TO92 [THT]"]
  LED1 = LED - 5mm [color="Red (633nm)" package="5 mm [THT]"]
  LED2 = LED - 5mm [color="Yellow (592nm)" package="5 mm [THT]"]
  LED3 = LED - 5mm [color="Green (555nm)" package="5 mm [THT]"]
  R2 = Resistor [tolerance=±5% resistance=220 package=THT]
  R3 = Resistor [tolerance=±5% resistance=220 package=THT]
  T1 = LM34 Temperature Sensor [package="TO92 [THT]"]

nets:
  N1: R1.leg1, Q1.C, LED1.cathode, LED2.cathode, LED3.cathode, R3.Pin_0, R3.Pin_1, T1.GND
  N2: R1.wiper, Part1.5V
  N3: R1.leg2, Part1.A0
  N4: M1.pin_1, Q1.B
  N5: M1.pin_2, Part1.3V3, T1.+Vs
  N6: Part1.A1, T1.Vout
  N7: Part1.D10_PWM/SS, R2.Pin_0
  N8: Part1.D11_PWM/MOSI, LED1.anode
  N9: Part1.D12/MISO, LED2.anode
  N10: Part1.D13/SCK, LED3.anode
  N11: Q1.E, R2.Pin_1
